# Fritzing sketch Untitled Sketch 2 (saved by Fritzing 0.9.6b)

parts:
  Part1 = Arduino Uno (Rev3) - ICSP
  ANT1 = Antenna
  U1 = RF-LINK_TX [package=rf-link_tx]

nets:
  N1: Part1.D13/SCK, U1.DATA
  GND: Part1.GND, U1.GND
  5V: Part1.5V, U1.+5V
  N2: ANT1.antenna_lead, U1.ANT
